# Fritzing sketch WifiEnergyMonitorFerraris8266 (saved by Fritzing 0.9.3b)
stripboards: 1

parts:
  R1 = Resistor [tolerance=±1% resistance=10k package=THT]
  R2 = Resistor [tolerance=±1% resistance=5k package=THT]
  C1 = Ceramic Capacitor [capacitance=100nF package="100 mil [THT, multilayer]"]
  U1 = NodeMCU V1.0
  R3 = Resistor [tolerance=±1% resistance=1k package=THT]
  R4 = Resistor [tolerance=±1% resistance=1k package=THT]
  J2 = RJ11 Jack [package=rj11-6]

nets:
  N1: R1.Pin_0, R2.Pin_1, U1.A0
  N2: R1.Pin_1, C1.0, U1.GND, J2.2
  N3: R2.Pin_0, J2.5
  N4: C1.1, U1.3V3, J2.3
  N5: U1.D1, R3.Pin_1
  N6: U1.D2, R4.Pin_1
  N7: R3.Pin_0, J2.6
  N8: R4.Pin_0, J2.4

custom parts:
  NodeMCU V1.0: ESP8266 based NodeMCU
